# Fritzing sketch midi_x0x_heart (saved by Fritzing 0.9.3b)
breadboards: 3

parts:
  IC2 = IC, DIP package, 8 pins [chip_label=6N138]
  R1 = Resistor [tolerance=±5% resistance=2.2k package=THT]
  R2 = Resistor [tolerance=±5% resistance=330 package=THT]
  Teensy++1 = Teensy++ 2.0
  U1 = MIDI_CONN_FEMALE_SUPPORT [package=din_5_female_support]
  R3 = Resistor [tolerance=±5% resistance=220 package=THT]
  U2 = MIDI_CONN_FEMALE_SUPPORT [package=din_5_female_support]
  R4 = Resistor [tolerance=±5% resistance=220 package=THT]
  R5 = Resistor [tolerance=±5% resistance=220 package=THT]
  IC4 = DIP - 14 pins [chip_label=MCP4922 package="DIP (Dual Inline) [THT]"]
  D1 = Diode [package=diode-1n4148]
  C1 = Ceramic Capacitor [capacitance=100nF package="100 mil [THT, multilayer]"]
  C7 = Tantalum Capacitor [capacitance=10µF package="100 mil [THT, tantalum]"]
  JP2 = Header 6 [package=molex-1x6-ra]

nets:
  N1: IC2.pin2, R3.Pin_1, D1.C
  N2: IC2.pin3, U1.MIDI_OUT, D1.A
  VSS: IC2.pin5, R1.Pin_0, Teensy++1.GND#0, U2.NC2, IC4.^LDAC, IC4.VSS, C1.0, C7.-, JP2.gnd
  N3: IC2.pin6, R2.Pin_0, Teensy++1.D3
  N4: IC2.pin7, R1.Pin_1
  VCC: IC2.pin8, R2.Pin_1, Teensy++1.VCC, R4.Pin_1, IC4.VDD, IC4.^SHDN, IC4.VREFB, IC4.VREFA, C1.1, C7.+, JP2.+5v
  N5: Teensy++1.D2, R5.Pin_0
  N6: U1.MIDI_IN, R3.Pin_0
  N7: U2.MIDI_IN, R4.Pin_0
  N8: U2.MIDI_OUT, R5.Pin_1

custom parts:
  DIP - 14 pins: A DIP stand-in part for whatever IC you want. With 14 pins on a 300mil dual inline package (DIP) footprint.
  Header 6: Header 6 Standard 6-pin 0.1 header. Use with straight break away headers (SKU : PRT-00116), right angle break away headers (PRT-00553), swiss pins (PRT-00743), machine pins (PRT-00117), and female headers (PRT-00115). Molex polarized connector foot print use with SKU : PRT-08094 with associated crimp pins and housings. NOTES ON THE VARIANTS LOCK and LOCK_LONGPADS... This footprint was designed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
